# Fritzing sketch PiZero-RTC-nrf24-rain-temperature-v4 (saved by Fritzing 0.9.3b)
perfboards: 1

parts:
  YL-83_-_Detection_Board4 = YL-83 Rain Sensor - Detection Board  # not connected
  DS5 = DS18B20 1-Wire Temperature Sensor Probe Cable  # not connected
  Raspberry_Pi_Zero4 = Raspberry Pi Zero
  YL-83_-_Control_Board5 = YL-83 Rain Sensor - Control Board  # not connected
  Part9 = NRF24L01+ Breakout Board  # not connected
  R13 = Resistor [tolerance=±5% resistance=4.7k package=THT]
  J7 = male pin header, 5 pins [form="♂ (male)"]
  J8 = female pin header, 4 pins [form="♀ (female)"]
  J9 = male pin header, 3 pins [form="♂ (male)"]
  J10 = female pin header, 4 pins [form="♀ (female)"]
  J11 = female pin header, 4 pins [form="♀ (female)"]
  J12 = male pin header, 3 pins [form="♂ (male)"]  # not connected

nets:
  3V3: Raspberry_Pi_Zero4.3v3, Raspberry_Pi_Zero4.3V3, J7.pin1, J10.pin4
  N1: Raspberry_Pi_Zero4.GPIO2, J7.pin2
  N2: Raspberry_Pi_Zero4.GPIO3, J7.pin3
  N3: Raspberry_Pi_Zero4.GPIO4, R13.Pin_0, J9.pin3
  N4: Raspberry_Pi_Zero4.GND, J7.pin5, J8.pin2, J9.pin2, J11.pin4
  N5: Raspberry_Pi_Zero4.GPIO22, J11.pin3
  N6: Raspberry_Pi_Zero4.GPIO10, J10.pin2
  N7: Raspberry_Pi_Zero4.GPIO9, J11.pin1
  N8: Raspberry_Pi_Zero4.GPIO11, J11.pin2
  N9: Raspberry_Pi_Zero4.GPIO26, J8.pin3
  N10: Raspberry_Pi_Zero4.5V, R13.Pin_1, J8.pin1, J9.pin1

notes:
  RTC
  Serial
  TX
  GND
  RX
  Chuva (1-wire)
  5V
  GND
  Data

custom parts:
  YL-83 Rain Sensor - Detection Board: The YL-83 is a rain sensor that has more resistance when dry and less resistance when wet. The module runs at 5V.
  YL-83 Rain Sensor - Control Board: The YL-83 is a rain sensor that has more resistance when dry and less resistance when wet. The module runs at 5V.
