# Fritzing sketch Sketch08-nano-chuva-temperatura-RTC-SD-semRF24 (saved by Fritzing 0.9.3b)
breadboards: 2

parts:
  LM1 = LM2596 [package=multiwatt15]
  Solar_pannel1 = solar_pannel
  YL-83_-_Control_Board2 = YL-83 Rain Sensor - Control Board
  YL-83_-_Detection_Board2 = YL-83 Rain Sensor - Detection Board
  DS3 = DS18B20 1-Wire Temperature Sensor Probe Cable  # not connected
  Part3 = Arduino Cellular Shield  # not connected
  Arduino1 = Arduino Pro Mini v13
  Part5 = Arduino Nano (Rev3.0)
  D3 = Rectifier Diode [part_number=1N4342 package="300 mil [THT]"]
  R3 = Resistor [tolerance=±5% resistance=4.7k package=THT]
  D4 = Rectifier Diode [part_number=1N4342 package="300 mil [THT]"]
  R4 = Resistor [tolerance=±5% resistance=4.7k package=THT]
  VCC2 = 4 x AAA Battery Mount
  ZS-042_RTC3 = ZS-042 RTC Module
  D5 = Rectifier Diode [part_number=1N4342 package="300 mil [THT]"]
  R5 = Resistor [tolerance=±5% resistance=4.7k package=THT]
  D6 = Rectifier Diode [part_number=1N4342 package="300 mil [THT]"]
  R6 = Resistor [tolerance=±5% resistance=4.7k package=THT]
  Part4 = MicroSD Card Module  # not connected

nets:
  N1: LM1.Vin, Solar_pannel1.aún_sin_nombre#1
  N2: LM1.GND, Solar_pannel1.aún_sin_nombre#0
  N3: YL-83_-_Control_Board2.POS, YL-83_-_Detection_Board2.POS
  N4: YL-83_-_Control_Board2.NEG, YL-83_-_Detection_Board2.NEG
  N5: Arduino1.A4, ZS-042_RTC3.SDA
  N6: Arduino1.A5, ZS-042_RTC3.SCL
  N7: Arduino1.RAW, VCC2.+
  VCC: Arduino1.VCC, ZS-042_RTC3.VCC
  N8: Arduino1.A1, D6.cathode, R6.Pin_0
  N9: Arduino1.A0, D5.cathode, R5.Pin_0
  N10: Arduino1.D7, D6.anode
  N11: Arduino1.D6_PWM, D5.anode
  N12: Part5.D6, D4.anode
  N13: Part5.D7, D3.anode
  N14: Part5.A1, D3.cathode, R3.Pin_0
  N15: Part5.A0, D4.cathode, R4.Pin_1
  N16: VCC2.-, ZS-042_RTC3.GND, R5.Pin_1, R6.Pin_1

notes:
  ** Micro SD **
  5V to 5V or Vcc
  GND to GND
  D13 to SCK
  D12 to MISO
  D11 to MOSI
  D10 to CS
  ** RTC **
  5V to 5V or Vcc
  GND to GND
  SDA to A4
  SCL to A5
  ** Rain Sensor **
  5V to 5V or Vcc
  GND to GND
  AO to A2
  DO to D2
  ** Temperature **
  5V to 5V or Vcc
  GND to GND
  White/Blue to D3

custom parts:
  LM2596: LM2596 switching voltage regulator
  solar_pannel: Solar pannel
  YL-83 Rain Sensor - Control Board: The YL-83 is a rain sensor that has more resistance when dry and less resistance when wet. The module runs at 5V.
  YL-83 Rain Sensor - Detection Board: The YL-83 is a rain sensor that has more resistance when dry and less resistance when wet. The module runs at 5V.
